// Logisim project Traffic light project.circ as structural Verilog: 1 circuit, main circuit main
module main (
);

  wire and_1_out, and_2_out, and_3_out, and_4_out, and_5_out, and_6_out, and_7_out, and_8_out, and_9_out,
       and_10_out, clock_1_out, d_ff_1_q, d_ff_1_qn, d_ff_2_q, d_ff_2_qn, d_ff_3_q, d_ff_3_qn, not_1_out,
       not_2_out, or_1_out, or_2_out, or_3_out, or_4_out, or_5_out;

  Clock clock_1 (.out(clock_1_out));
  and and_1 (and_1_out, d_ff_1_q, d_ff_2_qn, d_ff_3_qn);
  and and_2 (and_2_out, d_ff_1_qn, d_ff_2_q, d_ff_3_q);
  or or_1 (or_1_out, and_1_out, and_2_out);
  D_Flip_Flop d_ff_1 (.clk(clock_1_out), .D(or_1_out), .Q(d_ff_1_q), .Qn(d_ff_1_qn));  // open: preset, en, reset
  and and_3 (and_3_out, d_ff_1_qn, d_ff_2_qn, d_ff_3_q);
  and and_4 (and_4_out, d_ff_2_qn, d_ff_2_q, d_ff_3_qn);
  or or_2 (or_2_out, and_3_out, and_4_out);
  D_Flip_Flop d_ff_2 (.clk(clock_1_out), .D(or_2_out), .Q(d_ff_2_q), .Qn(d_ff_2_qn));  // open: preset, en, reset
  and and_5 (and_5_out, d_ff_2_qn, d_ff_3_qn);
  and and_6 (and_6_out, d_ff_1_qn, d_ff_3_qn);
  or or_3 (or_3_out, and_5_out, and_6_out);
  D_Flip_Flop d_ff_3 (.clk(clock_1_out), .D(or_3_out), .Q(d_ff_3_q), .Qn(d_ff_3_qn));  // open: preset, en, reset
  and and_7 (and_7_out, d_ff_1_qn, d_ff_2_q, d_ff_3_qn);
  and and_8 (and_8_out, d_ff_1_qn, d_ff_3_qn, d_ff_3_q);
  or or_4 (or_4_out, and_7_out, and_8_out);
  LED R1 (.in(not_1_out));
  not not_1 (not_1_out, or_4_out);
  LED Y1 (.in(and_7_out));
  LED G1 (.in(and_8_out));
  and and_9 (and_9_out, d_ff_3_q, d_ff_2_qn, d_ff_1_q);
  and and_10 (and_10_out, d_ff_3_qn, d_ff_2_qn, d_ff_1_q);
  LED G2 ();  // open: in
  or or_5 (or_5_out, and_9_out, and_10_out);
  LED Y2 ();  // open: in
  not not_2 (not_2_out, or_5_out);
  LED R2 ();  // open: in
endmodule
